# Fritzing sketch receiver (saved by Fritzing 0.9.3b)
breadboards: 1

parts:
  Part3 = Arduino Mega ADK (Rev3)
  Part4 = Bluetooth HC-05 Macho  # not connected
  BAT2 = Battery Holders [package=lipo-1100mAh]  # not connected
  RELAY1 = CAR RELAY [part_number=NVF4-2 package=THT]  # not connected

nets:
  GND: Part3.GND, Part3.VIN
