# Fritzing sketch transmitter_+carOS (saved by Fritzing 0.9.3b)
breadboards: 2

parts:
  Part3 = Arduino Mega ADK (Rev3)
  Part4 = Bluetooth HC-05 Macho
  BAT2 = Battery Holders [package=lipo-1100mAh]
  KY-1 = Keyes Relay [package=THT]
  J1 = Basic Servo
  VALVE1 = Plastic Solenoid Valve
  Power_plug1 = Power plug
  Part5 = Arduino Mega ADK (Rev3)
  BAT3 = Battery Holders [package=lipo-1100mAh]
  MPX2 = MPX2010 pressure sensor [part_number=MPX]
  HC-1 = HC-12 Module
  Antenna1 = HC-12 Antenna
  HC-2 = HC-12 Module
  Antenna2 = HC-12 Antenna

nets:
  N1: Part3.D17/RX2, Part4.RXD
  N2: Part3.D16/TX2, Part4.TXD
  N3: Part3.D15/RX3, HC-2.RXD
  N4: Part3.D14/TX3, HC-2.TXD
  GND: Part3.GND, Part3.VIN, Part4.GND, BAT2.-, KY-1.ground, HC-2.GND
  N5: Part3.D4_PWM, J1.pulse
  N6: Part3.D5_PWM, KY-1.signal
  VCC: Part4.VCC, BAT2.+, KY-1.power, HC-2.VCC
  N7: KY-1.C, Power_plug1.GND
  N8: KY-1.NO, VALVE1.no_name_yet#2
  N9: VALVE1.no_name_yet#1, Power_plug1.VCC
  N10: Part5.A8, MPX2.GND
  N11: Part5.D15/RX3, HC-1.RXD
  N12: Part5.D14/TX3, HC-1.TXD
  N13: BAT3.+, MPX2.Vs, HC-1.VCC
  N14: BAT3.-, MPX2.V_out_-, HC-1.GND
  N15: HC-1.ANT, Antenna1.ANT
  N16: HC-2.ANT, Antenna2.ANT

custom parts:
  Keyes Relay: The Keyes 5V relay module is suitable for SCM development, home appliance control. It uses a 5V~12V TIL control signal which can control DC / AC signal.
  HC-12 Module: HC-12 433Mhz Module
  HC-12 Antenna: Antenna for HC-12 433Mhz Module
